# Fritzing sketch PCB Design (saved by Fritzing 0.9.3b)
circuit board: 6.0223cm x 2.34859cm
breadboards: 1

parts:
  T1 = LM35 Temperature Sensor [package="TO92 [THT]"]
  J1 = male pin header, 3 pins [form="♂ (male)"]
  Raspberry_Pi_1 = Raspberry Pi 3 [part_number=RPI-3-V1.2]

nets:
  N1: T1.+Vs, J1.pin2, Raspberry_Pi_1.3v3
  N2: T1.Vout, J1.pin3, Raspberry_Pi_1.GIPO4
  GND: T1.GND, J1.pin1, Raspberry_Pi_1.GND

notes:
  Matthew Phillip
